// Logisim project p1.circ as structural Verilog: 2 circuits, main circuit main
module main (
  input  X,
  input  Y,
  input  Z,
  output \output 
);

  wire not_1_out, not_2_out, not_3_out, or_1_out, or_2_out;

  not not_1 (not_1_out, Y);
  not not_2 (not_2_out, Z);
  not not_3 (not_3_out, X);
  or or_1 (or_1_out, X, not_1_out, Z);
  or or_2 (or_2_out, not_3_out, Y, not_2_out);
  and and_1 (\output , or_1_out, or_2_out);

  // Notes on the sheet:
  //   P1 (A)
endmodule

module P1__B (
  input  X,
  input  Y,
  input  Z,
  input  F,
  output \output 
);

  wire and_1_out, and_2_out, and_3_out, and_4_out, not_1_out, not_2_out, not_3_out, not_4_out;

  not not_1 (not_1_out, X);
  not not_2 (not_2_out, Y);
  not not_3 (not_3_out, Z);
  not not_4 (not_4_out, F);
  and and_1 (and_1_out, not_1_out, not_2_out, F);
  and and_2 (and_2_out, not_2_out, not_3_out, F);
  and and_3 (and_3_out, Z, Y, not_4_out);
  and and_4 (and_4_out, X, Y, not_4_out);
  or or_1 (\output , and_1_out, and_2_out, and_3_out, and_4_out);

  // Notes on the sheet:
  //   dog
  //   goat
  //   cabbage
  //   farmer
  //   P1 (B)
endmodule
