// Logisim project p6.circ as structural Verilog: 2 circuits, main circuit main
module main (
  input  X,
  input  Y,
  input  Z,
  input  W
);

  wire p6_1_a, p6_1_b, p6_1_c, p6_1_d, p6_1_e, p6_1_f, p6_1_g;

  p6 p6_1 (
    .X(X), .Y(Y), .Z(Z), .W(W), .A(p6_1_a), .B(p6_1_b), .C(p6_1_c), .D(p6_1_d), .E(p6_1_e), .F(p6_1_f),
    .G(p6_1_g));
  _7_Segment_Display u_7_segment_display_1 (
    .g(p6_1_g), .f(p6_1_f), .a(p6_1_a), .b(p6_1_b), .e(p6_1_e), .d(p6_1_d), .c(p6_1_c));  // open: dp
endmodule

module p6 (
  input  X,
  input  Y,
  input  Z,
  input  W,
  output A,
  output B,
  output C,
  output D,
  output E,
  output F,
  output G
);

  wire not_1_out, not_2_out, not_3_out, not_4_out, or_1_out, or_2_out, or_3_out, or_4_out, or_5_out,
       or_6_out, or_7_out, or_8_out, or_9_out, or_10_out, or_11_out, or_12_out, or_13_out, or_14_out,
       or_15_out, or_16_out, or_17_out, or_18_out, or_19_out, or_20_out, or_21_out, or_22_out, or_23_out,
       or_24_out, or_25_out;

  not not_1 (not_1_out, X);
  not not_2 (not_2_out, Y);
  not not_3 (not_3_out, Z);
  not not_4 (not_4_out, W);
  or or_1 (or_1_out, X, Y, Z, not_4_out);
  or or_2 (or_2_out, X, not_2_out, Z, W);
  or or_3 (or_3_out, not_1_out, Y, not_3_out, not_4_out);
  or or_4 (or_4_out, not_1_out, not_2_out, Z, not_4_out);
  or or_5 (or_5_out, X, not_2_out, Z, not_4_out);
  or or_6 (or_6_out, not_2_out, not_3_out, W);
  or or_7 (or_7_out, not_1_out, not_3_out, not_4_out);
  or or_8 (or_8_out, not_1_out, not_2_out, W);
  or or_9 (or_9_out, X, Y, not_3_out, W);
  or or_10 (or_10_out, not_1_out, not_2_out, W);
  or or_11 (or_11_out, not_1_out, not_2_out, not_3_out);
  or or_12 (or_12_out, not_1_out, Y, not_3_out, W);
  or or_13 (or_13_out, X, not_2_out, Z, W);
  or or_14 (or_14_out, X, Y, Z, not_4_out);
  or or_15 (or_15_out, not_2_out, not_3_out, not_4_out);
  or or_16 (or_16_out, Y, Z, not_4_out);
  or or_17 (or_17_out, X, not_2_out, Z);
  or or_18 (or_18_out, X, not_4_out);
  or or_19 (or_19_out, not_1_out, not_2_out, Z, not_4_out);
  or or_20 (or_20_out, X, Y, not_3_out);
  or or_21 (or_21_out, X, Y, not_4_out);
  or or_22 (or_22_out, X, not_3_out, not_4_out);
  or or_23 (or_23_out, X, Y, Z);
  or or_24 (or_24_out, X, not_2_out, not_3_out, not_4_out);
  or or_25 (or_25_out, not_1_out, not_2_out, Z, W);
  and and_1 (C, or_9_out, or_10_out, or_11_out);
  and and_2 (D, or_12_out, or_13_out, or_14_out, or_15_out);
  and and_3 (E, or_16_out, or_17_out, or_18_out);
  and and_4 (F, or_19_out, or_20_out, or_21_out, or_22_out);
  and and_5 (G, or_23_out, or_24_out, or_25_out);
  and and_6 (A, or_1_out, or_2_out, or_3_out, or_4_out);
  and and_7 (B, or_5_out, or_6_out, or_7_out, or_8_out);
endmodule
