// Logisim project p1.circ as structural Verilog: 1 circuit, main circuit main
module main (
  input  w,
  input  x,
  input  y,
  input  z,
  output \output 
);

  wire and_1_out, and_2_out, and_3_out, not_1_out, not_2_out, not_3_out, not_4_out;

  not not_1 (not_1_out, z);
  not not_2 (not_2_out, w);
  not not_3 (not_3_out, x);
  not not_4 (not_4_out, y);
  and and_1 (and_1_out, w, not_3_out, not_4_out);
  and and_2 (and_2_out, x, y);
  and and_3 (and_3_out, not_2_out, y, not_1_out);
  or or_1 (\output , and_1_out, and_2_out, and_3_out);
endmodule
