// Logisim project p10.circ as structural Verilog: 1 circuit, main circuit main
module main (
  input  b0,
  input  a0,
  input  b1,
  input  a1,
  output s0,
  output s1,
  output c
);

  wire and_1_out, and_2_out, and_3_out, and_4_out, and_5_out, and_6_out, and_7_out, and_8_out, and_9_out,
       and_10_out, and_11_out, not_1_out, not_2_out, not_3_out, not_4_out, not_5_out, not_6_out, not_7_out,
       not_8_out, not_9_out, not_10_out, not_11_out, not_12_out;

  not not_1 (not_1_out, b0);
  not not_2 (not_2_out, a0);
  not not_3 (not_3_out, b0);
  not not_4 (not_4_out, b1);
  not not_5 (not_5_out, a0);
  not not_6 (not_6_out, b1);
  not not_7 (not_7_out, b0);
  not not_8 (not_8_out, a1);
  not not_9 (not_9_out, a0);
  not not_10 (not_10_out, a1);
  not not_11 (not_11_out, b1);
  not not_12 (not_12_out, a1);
  and and_1 (and_1_out, not_1_out, a0);
  and and_2 (and_2_out, b0, not_2_out);
  and and_3 (and_3_out, not_5_out, not_6_out, a1);
  and and_4 (and_4_out, not_9_out, b1, not_10_out);
  and and_5 (and_5_out, b0, a0, not_11_out, not_12_out);
  and and_6 (and_6_out, b1, a1);
  and and_7 (and_7_out, b0, a0, a1);
  and and_8 (and_8_out, b0, a0, b1);
  and and_9 (and_9_out, not_7_out, b1, not_8_out);
  and and_10 (and_10_out, not_3_out, not_4_out, a1);
  and and_11 (and_11_out, b0, a0, b1, a1);
  or or_1 (s0, and_1_out, and_2_out);
  or or_2 (s1, and_10_out, and_3_out, and_9_out, and_4_out, and_5_out, and_11_out);
  or or_3 (c, and_6_out, and_7_out, and_8_out);
endmodule
