// Logisim project p3(b).circ as structural Verilog: 2 circuits, main circuit P3(b)
module P3_b (
  input  a3,
  input  b3,
  input  a2,
  input  b2,
  input  a1,
  input  b1,
  input  a0,
  input  [3:0] A,
  input  b0,
  input  [3:0] B,
  input  s0,
  input  s0_2,
  output out_13,
  output out_14,
  output out_15,
  output out_16,
  output [3:0] C
);

  _2_to_1_multiplexer u_2_to_1_multiplexer_1 (.I0(a3), .I1(b3), .S0(s0), .Y(out_13));
  _2_to_1_multiplexer u_2_to_1_multiplexer_2 (.I0(a2), .I1(b2), .S0(s0), .Y(out_14));
  _2_to_1_multiplexer u_2_to_1_multiplexer_3 (.I0(a1), .I1(b1), .S0(s0), .Y(out_15));
  _2_to_1_multiplexer u_2_to_1_multiplexer_4 (.I0(a0), .I1(b0), .S0(s0), .Y(out_16));
  Multiplexer #(.width(4)) multiplexer_1 (.in0(A), .in1(B), .out(C), .sel(s0_2));  // open: en
endmodule

module _2_to_1_multiplexer (
  input  I0,
  input  I1,
  input  S0,
  output Y
);

  wire and_1_out, and_2_out, not_1_out;

  not not_1 (not_1_out, S0);
  and and_1 (and_1_out, I0, not_1_out);
  and and_2 (and_2_out, I1, S0);
  or or_1 (Y, and_1_out, and_2_out);
endmodule
