// Logisim project p3.circ as structural Verilog: 5 circuits, main circuit main
module main (
  input  A,
  input  B,
  output \output 
);

  wire not_1_out;

  not not_1 (not_1_out, B);
  or or_1 (\output , A, not_1_out);

  // Notes on the sheet:
  //   P3 (A)
endmodule

module p3_b (
  input  A,
  input  B,
  input  C,
  output Y
);

  wire and_1_out, and_2_out, not_1_out, not_2_out, not_3_out;

  not not_1 (not_1_out, A);
  not not_2 (not_2_out, B);
  not not_3 (not_3_out, C);
  and and_1 (and_1_out, not_1_out, not_2_out, not_3_out);
  and and_2 (and_2_out, A, B, C);
  or or_1 (Y, and_1_out, and_2_out);

  // Notes on the sheet:
  //   p3(b)
endmodule

module p3_c (
  input  A,
  input  B,
  input  C,
  output \output 
);

  wire not_1_out, not_2_out, not_3_out, or_1_out, or_2_out;

  not not_1 (not_1_out, A);
  not not_2 (not_2_out, B);
  not not_3 (not_3_out, C);
  or or_1 (or_1_out, A, not_3_out);
  or or_2 (or_2_out, not_1_out, not_2_out, C);
  and and_1 (\output , or_1_out, or_2_out);

  // Notes on the sheet:
  //   p3(c)
endmodule

module p3_d (
  input  A,
  input  B,
  input  C,
  input  D,
  output OUTPUT
);

  wire not_1_out, not_2_out, not_3_out, or_1_out, or_2_out, or_3_out;

  not not_1 (not_1_out, A);
  not not_2 (not_2_out, B);
  not not_3 (not_3_out, D);
  or or_1 (or_1_out, A, not_2_out);
  or or_2 (or_2_out, not_2_out, C);
  or or_3 (or_3_out, not_1_out, not_3_out);
  and and_1 (OUTPUT, or_1_out, or_2_out, or_3_out);

  // Notes on the sheet:
  //   P3(D)
endmodule

module p3_e (
  input  A,
  input  B,
  input  C,
  input  D,
  output Y
);

  wire and_1_out, and_2_out, and_3_out, and_4_out, and_5_out, and_6_out, and_7_out, and_8_out, not_1_out,
       not_2_out, not_3_out, not_4_out;

  not not_1 (not_1_out, A);
  not not_2 (not_2_out, B);
  not not_3 (not_3_out, C);
  not not_4 (not_4_out, D);
  and and_1 (and_1_out, not_1_out, not_2_out, not_3_out, not_4_out);
  and and_2 (and_2_out, not_1_out, not_2_out, C, D);
  and and_3 (and_3_out, not_1_out, B, not_3_out, D);
  and and_4 (and_4_out, not_1_out, B, C, not_4_out);
  and and_5 (and_5_out, A, not_2_out, D, not_3_out);
  and and_6 (and_6_out, A, not_2_out, C, not_4_out);
  and and_7 (and_7_out, A, B, not_3_out, not_4_out);
  and and_8 (and_8_out, A, B, C, D);
  or or_1 (Y, and_1_out, and_2_out, and_3_out, and_4_out, and_5_out, and_6_out, and_7_out, and_8_out);

  // Notes on the sheet:
  //   P3(E)
endmodule
