// Logisim project p4 (2).circ as structural Verilog: 1 circuit, main circuit main
module main (
  input  A,
  input  B,
  input  C,
  input  D,
  input  s0,
  input  s1,
  input  s2,
  input  s3,
  output OUTPUT
);

  wire and_1_out, and_2_out, and_3_out, and_4_out, not_1_out, not_2_out, not_3_out, not_4_out;

  not not_1 (not_1_out, s0);
  not not_2 (not_2_out, s1);
  not not_3 (not_3_out, s2);
  not not_4 (not_4_out, s3);
  and and_1 (and_1_out, A, s0, not_2_out, not_3_out, not_4_out);
  and and_2 (and_2_out, B, not_1_out, s1, not_3_out, not_4_out);
  and and_3 (and_3_out, C, not_1_out, not_2_out, s2, not_4_out);
  and and_4 (and_4_out, D, not_1_out, not_2_out, not_3_out, s3);
  or or_1 (OUTPUT, and_1_out, and_2_out, and_3_out, and_4_out);
endmodule
