// Logisim project p4.circ as structural Verilog: 1 circuit, main circuit main
module main (
  input  A,
  input  B,
  input  C,
  input  D,
  input  s0,
  input  s1,
  input  s2,
  input  s3,
  output OUTPUT
);

  wire and_1_out, and_2_out, and_3_out, and_4_out;

  buf and_1 (and_1_out, A);  // AND_Gate
  buf and_2 (and_2_out, B);  // AND_Gate
  buf and_3 (and_3_out, C);  // AND_Gate
  and and_4 (and_4_out, D, s3);
  or or_1 (OUTPUT, and_1_out, and_2_out, and_3_out, and_4_out);
endmodule
