// Logisim project p5 (2).circ as structural Verilog: 1 circuit, main circuit main
module main (
  input  [3:0] A,
  input  [3:0] B,
  input  [3:0] S0,
  output [3:0] OUTPUT
);

  wire [3:0] and_1_out, and_2_out, not_1_out;

  assign not_1_out = ~S0;  // NOT_Gate not_1, 4 bits wide
  assign and_1_out = A & not_1_out;  // AND_Gate and_1, 4 bits wide
  assign and_2_out = B & S0;  // AND_Gate and_2, 4 bits wide
  assign OUTPUT = and_1_out | and_2_out;  // OR_Gate or_1, 4 bits wide

  // Notes on the sheet:
  //   C
endmodule
