// Logisim project p6.circ as structural Verilog: 1 circuit, main circuit main
module main (
  input  [3:0] A,
  input  [3:0] B,
  input  [3:0] C,
  input  [3:0] D,
  input  [3:0] S0,
  input  [3:0] S1,
  output [3:0] OUTPUT
);

  wire [3:0] and_1_out, and_2_out, and_3_out, and_4_out, not_1_out, not_2_out, not_3_out, not_4_out;

  assign not_1_out = ~S0;  // NOT_Gate not_1, 4 bits wide
  assign not_2_out = ~S1;  // NOT_Gate not_2, 4 bits wide
  assign not_3_out = ~S1;  // NOT_Gate not_3, 4 bits wide
  assign not_4_out = ~S0;  // NOT_Gate not_4, 4 bits wide
  assign and_1_out = A & not_1_out & not_2_out;  // AND_Gate and_1, 4 bits wide
  assign and_2_out = B & S0 & not_3_out;  // AND_Gate and_2, 4 bits wide
  assign and_3_out = C & not_4_out & S1;  // AND_Gate and_3, 4 bits wide
  assign and_4_out = D & S0 & S1;  // AND_Gate and_4, 4 bits wide
  assign OUTPUT = and_1_out | and_2_out | and_3_out | and_4_out;  // OR_Gate or_1, 4 bits wide
endmodule
