// Logisim project p8.circ as structural Verilog: 1 circuit, main circuit main
module main (
  input  A,
  input  B,
  input  C,
  input  D,
  input  E,
  input  F,
  input  G,
  input  H,
  input  I,
  input  J,
  input  K,
  input  L,
  input  M,
  input  N,
  input  O,
  input  P,
  input  S0,
  input  S1,
  input  S2,
  input  S3,
  output OUTPUT
);

  wire and_1_out, and_2_out, and_3_out, and_4_out, and_5_out, and_6_out, and_7_out, and_8_out, and_9_out,
       and_10_out, and_11_out, and_12_out, and_13_out, and_14_out, and_15_out, and_16_out, not_1_out,
       not_2_out, not_3_out, not_4_out;

  not not_1 (not_1_out, S1);
  not not_2 (not_2_out, S2);
  not not_3 (not_3_out, S3);
  not not_4 (not_4_out, S0);
  and and_1 (and_1_out, A, not_1_out, not_4_out, not_2_out, not_3_out);
  and and_2 (and_2_out, B, not_1_out, not_4_out, not_2_out, S3);
  and and_3 (and_3_out, C, not_1_out, not_4_out, S2, not_3_out);
  and and_4 (and_4_out, D, not_1_out, not_4_out, S2, S3);
  and and_5 (and_5_out, E, S1, not_4_out, not_2_out, not_3_out);
  and and_6 (and_6_out, F, S1, not_4_out, not_2_out, S3);
  and and_7 (and_7_out, G, S1, not_4_out, S2, not_3_out);
  and and_8 (and_8_out, H, S1, not_4_out, S2, S3);
  and and_9 (and_9_out, I, not_1_out, S0, not_2_out, not_3_out);
  and and_10 (and_10_out, J, not_1_out, S0, not_2_out, S3);
  and and_11 (and_11_out, K, not_1_out, S0, S2, not_3_out);
  and and_12 (and_12_out, L, not_1_out, S0, S2, S3);
  and and_13 (and_13_out, M, S1, S0, not_2_out, not_3_out);
  and and_14 (and_14_out, N, S1, S0, not_2_out, S3);
  and and_15 (and_15_out, O, S1, S0, S2, not_3_out);
  and and_16 (and_16_out, P, S1, S0, S2, S3);
  or or_1 (OUTPUT, and_1_out, and_2_out, and_3_out, and_4_out, and_5_out, and_6_out, and_7_out, and_8_out, and_9_out, and_10_out, and_11_out, and_12_out, and_13_out, and_14_out, and_15_out, and_16_out);
endmodule
